// Logisim project TrabalhoCircuitoMultiplicador.circ as structural Verilog: 4 circuits, main circuit main
module main (
  input  A3,
  input  A2,
  input  A1,
  input  A0,
  input  B0,
  input  B1,
  input  B2,
  input  B3
);

  wire bcd_to_7_segment_decoder_1_p1, bcd_to_7_segment_decoder_2_p1, binary_to_bcd_converter_1_p4;
  wire [7:0] multiply_1_s0;

  MULTIPLY multiply_1 (
    .S1(multiply_1_s0[1]), .S0(multiply_1_s0[0]), .S7(multiply_1_s0[7]), .S6(multiply_1_s0[6]),
    .S5(multiply_1_s0[5]), .S4(multiply_1_s0[4]), .S3(multiply_1_s0[3]), .S2(multiply_1_s0[2]), .A1(A1),
    .A0(A0), .B2(B2), .B0(B0), .B1(B1), .B3(B3), .A3(A3), .A2(A2));
  _7_Segment_Display u_7_segment_display_1 ();  // open: g, f, a, b, e, d, c, dp
  // BCD_to_7_Segment_decoder bcd_to_7_segment_decoder_1: pin names not known; wires that end beside it: bcd_to_7_segment_decoder_1_p1
  _7_Segment_Display u_7_segment_display_2 ();  // open: g, f, a, b, e, d, c, dp
  // BCD_to_7_Segment_decoder bcd_to_7_segment_decoder_2: pin names not known; wires that end beside it: bcd_to_7_segment_decoder_2_p1
  // Binary_to_BCD_converter #(.binvalue(8)) binary_to_bcd_converter_1: pin names not known; wires that end beside it: multiply_1_s0, bcd_to_7_segment_decoder_1_p1, bcd_to_7_segment_decoder_2_p1, binary_to_bcd_converter_1_p4
  _7_Segment_Display u_7_segment_display_3 ();  // open: g, f, a, b, e, d, c, dp
  // BCD_to_7_Segment_decoder bcd_to_7_segment_decoder_3: pin names not known; wires that end beside it: binary_to_bcd_converter_1_p4
endmodule

module FULLADD (
  input  A,
  input  B,
  input  Cin,
  output SUM,
  output COut
);

  wire and_1_out, and_2_out, xor_1_out;

  xor xor_1 (xor_1_out, B, A);
  and and_1 (and_1_out, Cin, xor_1_out);
  and and_2 (and_2_out, B, A);
  xor xor_2 (SUM, xor_1_out, Cin);
  or or_1 (COut, and_1_out, and_2_out);
endmodule

module HALFADD (
  input  A,
  input  B,
  output Carry,
  output SUM
);

  and and_1 (Carry, B, A);
  xor xor_1 (SUM, B, A);
endmodule

module MULTIPLY (
  input  A3,
  input  A2,
  input  A1,
  input  A0,
  input  B0,
  input  B1,
  input  B2,
  input  B3,
  output S0,
  output S1,
  output S7,
  output S6,
  output S5,
  output S4,
  output S3,
  output S2
);

  wire and_1_out, and_2_out, and_3_out, and_4_out, and_5_out, and_6_out, and_7_out, and_8_out, and_9_out,
       and_10_out, and_11_out, and_12_out, and_13_out, and_14_out, and_15_out, fulladd_2_cout,
       fulladd_3_cout, fulladd_3_sum, fulladd_4_cout, fulladd_4_sum, fulladd_5_cout, fulladd_6_cout,
       fulladd_6_sum, fulladd_7_cout, fulladd_7_sum, fulladd_8_cout, fulladd_8_sum, halfadd_1_carry,
       halfadd_1_sum, halfadd_2_carry, halfadd_3_carry, halfadd_4_carry;

  and and_1 (and_1_out, A3, B3);
  FULLADD fulladd_1 (.COut(S7), .SUM(S6), .Cin(fulladd_2_cout), .A(and_1_out), .B(fulladd_3_cout));
  and and_2 (and_2_out, A2, B3);
  FULLADD fulladd_2 (.COut(fulladd_2_cout), .SUM(S5), .Cin(fulladd_5_cout), .A(and_2_out), .B(fulladd_3_sum));
  and and_3 (and_3_out, A3, B2);
  FULLADD fulladd_3 (
    .COut(fulladd_3_cout), .SUM(fulladd_3_sum), .Cin(fulladd_4_cout), .A(and_3_out), .B(halfadd_1_carry));
  and and_4 (and_4_out, A3, B1);
  HALFADD halfadd_1 (.Carry(halfadd_1_carry), .SUM(halfadd_1_sum), .A(fulladd_6_cout), .B(and_4_out));
  and and_5 (and_5_out, B2, A2);
  FULLADD fulladd_4 (
    .COut(fulladd_4_cout), .SUM(fulladd_4_sum), .Cin(fulladd_7_cout), .A(and_5_out), .B(halfadd_1_sum));
  and and_6 (and_6_out, B3, A1);
  FULLADD fulladd_5 (.COut(fulladd_5_cout), .SUM(S4), .Cin(halfadd_2_carry), .A(and_6_out), .B(fulladd_4_sum));
  and and_7 (and_7_out, A3, B0);
  and and_8 (and_8_out, B1, A2);
  FULLADD fulladd_6 (.COut(fulladd_6_cout), .SUM(fulladd_6_sum), .Cin(fulladd_8_cout), .A(and_8_out), .B(and_7_out));
  and and_9 (and_9_out, B2, A1);
  FULLADD fulladd_7 (
    .COut(fulladd_7_cout), .SUM(fulladd_7_sum), .Cin(halfadd_3_carry), .A(and_9_out), .B(fulladd_6_sum));
  and and_10 (and_10_out, B3, A0);
  HALFADD halfadd_2 (.Carry(halfadd_2_carry), .SUM(S3), .A(and_10_out), .B(fulladd_7_sum));
  and and_11 (and_11_out, A2, B0);
  and and_12 (and_12_out, B1, A1);
  FULLADD fulladd_8 (.COut(fulladd_8_cout), .SUM(fulladd_8_sum), .Cin(halfadd_4_carry), .A(and_12_out), .B(and_11_out));
  and and_13 (and_13_out, B2, A0);
  HALFADD halfadd_3 (.Carry(halfadd_3_carry), .SUM(S2), .A(and_13_out), .B(fulladd_8_sum));
  and and_14 (and_14_out, A1, B0);
  and and_15 (and_15_out, B1, A0);
  HALFADD halfadd_4 (.Carry(halfadd_4_carry), .SUM(S1), .A(and_15_out), .B(and_14_out));
  and and_16 (S0, A0, B0);
endmodule
